# Fritzing sketch skematik (saved by Fritzing 0.9.3b)
breadboards: 1

parts:
  U1 = NodeMCU V3.0
  Part1 = INA219 High Side DC Current Sensor Breakout [part_number=904]
  R3 = Resistor [tolerance=±5% resistance=100 package=THT]
  R2 = Resistor [tolerance=±5% resistance=100 package=THT]
  R6 = Resistor [tolerance=±5% resistance=2.2k package=THT]
  R1 = Resistor [tolerance=±5% resistance=100 package=THT]
  Part2 = INA219 High Side DC Current Sensor Breakout [part_number=904]
  Part3 = INA219 High Side DC Current Sensor Breakout [part_number=904]
  Part4 = INA219 High Side DC Current Sensor Breakout [part_number=904]
  Part5 = INA219 High Side DC Current Sensor Breakout [part_number=904]
  Part6 = INA219 High Side DC Current Sensor Breakout [part_number=904]
  Part7 = Adafruit TCA9548A
  R5 = Resistor [tolerance=±5% resistance=500 package=THT]
  Part8 = INA219 High Side DC Current Sensor Breakout [part_number=904]
  Part9 = INA219 High Side DC Current Sensor Breakout [part_number=904]
  R4 = Resistor [tolerance=±5% resistance=2.2k package=THT]
  R7 = Resistor [tolerance=±5% resistance=2.2k package=THT]
  VCC1 = 4 x AAA Battery Mount

nets:
  N1: U1.D1, Part7.INPUTSCL
  N2: U1.D2, Part7.INPUTSDA
  VCC: U1.3V3, Part1.VCC, Part5.VCC, Part6.VCC, Part7.VCC
  GND: U1.GND, Part1.GND, Part5.GND, Part6.GND, Part7.GND, Part7.A0, Part7.A1, Part7.A2
  N3: Part1.VIN-, R1.Pin_1
  N4: Part1.VIN+, VCC1.+
  N5: Part1.SCL, Part7.0SCL
  N6: Part1.SDA, Part7.0SDA
  N7: R3.Pin_0, Part4.VIN+
  N8: R3.Pin_1, Part5.VIN-
  N9: R2.Pin_0, Part5.VIN+
  N10: R2.Pin_1, Part6.VIN-
  N11: R6.Pin_1, Part2.VIN-
  N12: R1.Pin_0, Part3.VIN+, Part6.VIN+
  N13: Part2.SCL, Part7.5SCL
  N14: Part2.SDA, Part7.5SDA
  N15: Part3.VIN-, Part9.VIN+
  N16: Part3.SCL, Part7.4SCL
  N17: Part3.SDA, Part7.4SDA
  N18: Part4.VIN-, R4.Pin_1
  N19: Part4.SCL, Part7.3SCL
  N20: Part4.SDA, Part7.3SDA
  N21: Part5.SCL, Part7.2SCL
  N22: Part5.SDA, Part7.2SDA
  N23: Part6.SCL, Part7.1SCL
  N24: Part6.SDA, Part7.1SDA
  N25: Part7.6SDA, Part8.SDA
  N26: Part7.6SCL, Part8.SCL
  N27: Part7.7SDA, Part9.SDA
  N28: Part7.7SCL, Part9.SCL
  N29: R5.Pin_1, Part8.VIN-
  N30: Part9.VIN-, R7.Pin_1
  N31: R4.Pin_0, R7.Pin_0, VCC1.-

custom parts:
  NodeMCU V3.0: ESP8266 based NodeMCU
  INA219 High Side DC Current Sensor Breakout: This breakout board will solve all your power-monitoring problems. Instead of struggling with two multimeters, you can just use the handy INA219B chip on this breakout to both measure both the high side voltage and DC current draw over I2C with 1% precision. Most current-measuring devices such as our current panel meter are only good for low side measuring. That means that unless you want to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
  Adafruit TCA9548A: You just found the perfect I2C sensor, and you want to wire up two or three or more of them to your Arduino when you realize "Uh oh, this chip has a fixed I2C address, and from what I know about I2C, you cannot have two devices with the same address on the same SDA/SCL pins!" Are you out of luck? You would be, if you didn't have this ultra-cool TCA9548A 1-to-8 I2C multiplexer! Finally, a way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
